// Digital circuit CPU.dig as structural Verilog
module CPU (
  input  clk
);

  wire alu_op, B, CI, not_1_out, \reg , we, wm, wreg;
  wire [2:0] funct3;
  wire [6:0] funct7, opcode;
  wire [23:0] rd, rs1, rs2;
  wire [31:0] add_1_s, BR_da, BR_db, calc_imm_1_imm, multiplexer_1_out, PC_q;
  wire [31:8] undriven;

  Register #(.Bits(32)) PC (.D(add_1_s), .C(clk), .en(1'b1), .Q(PC_q));
  Add #(.Bits(32)) add_1 (.a({undriven, 8'h4}), .b(PC_q), .s(add_1_s));  // open: c_i, c_o
  ROM #(.AddrBits(24), .Bits(32)) IM (
    .A(PC_q[23:0]), .sel(1'b1), .D({funct7, rs2[4:0], rs1[4:0], funct3, rd[4:0], opcode}));
  calc_imm calc_imm_1 (
    .instr({funct7, rs2[4:0], rs1[4:0], funct3, rd[4:0], opcode}), .imm(calc_imm_1_imm));  // open: opcode
  // CU cu_1: pin names not known; wires that end beside it: B, wm, \reg , CI, alu_op, opcode, wreg
  RegisterFile #(.AddrBits(24), .Bits(32)) BR (
    .we(wreg), .Rw(rd), .C(clk), .Ra(rs1), .Rb(rs2), .Da(BR_da), .Db(BR_db));  // open: Din
  Multiplexer #(.Bits(32)) multiplexer_1 (.sel(CI), .in_0(BR_db), .in_1(calc_imm_1_imm), .out(multiplexer_1_out));
  ULA ula_1 (.op1(BR_da), .op2(multiplexer_1_out));  // open: controle, s
  not not_1 (not_1_out, clk);
  RAMDualPort #(.AddrBits(24), .Bits(32)) MD (.str(we), .C(not_1_out));  // open: A, Din, ld, D
  // Pins of 24 and 32 bits meet at PC_q
  // Pins of 8 and 32 bits meet at {undriven, 8'h4}
  // Pins of 5 and 24 bits meet at rd
  // Pins of 5 and 24 bits meet at rs1
  // Pins of 5 and 24 bits meet at rs2
endmodule
